# Fritzing sketch ckt_diagram (saved by Fritzing 0.9.2b)
breadboards: 2

parts:
  Part1 = Bluetooth HC-05 Macho
  TCRT9 = TCRT5000 sensor module [part_number=151608]
  TCRT10 = TCRT5000 sensor module [part_number=151608]
  TCRT11 = TCRT5000 sensor module [part_number=151608]
  TCRT12 = TCRT5000 sensor module [part_number=151608]
  TCRT13 = TCRT5000 sensor module [part_number=151608]
  TCRT14 = TCRT5000 sensor module [part_number=151608]
  TCRT15 = TCRT5000 sensor module [part_number=151608]
  TCRT16 = TCRT5000 sensor module [part_number=151608]
  Part2 = Arduino Nano (Rev3.0)
  S1 = H-Bridge with L298N
  U1 = LIPO-110mAh [package=lipo-110]
  U2 = LIPO-110mAh [package=lipo-110]
  U3 = LIPO-110mAh [package=lipo-110]
  M2 = DC Motor
  M3 = DC Motor

nets:
  N1: Part1.TXD, Part2.D10
  N2: Part1.RXD, Part2.D11/MOSI
  VCC: Part1.VCC, Part2.VIN, S1.12V, U3.+
  GND: Part1.GND, TCRT9.D-, TCRT9.T-, TCRT10.D-, TCRT10.T-, TCRT11.D-, TCRT11.T-, TCRT12.D-, TCRT12.T-, TCRT13.D-, TCRT13.T-, TCRT14.D-, TCRT14.T-, TCRT15.D-, TCRT15.T-, TCRT16.D-, TCRT16.T-, Part2.GND, S1.GND, U1.-
  N3: TCRT9.D+, TCRT10.D+, TCRT11.D+, TCRT12.D+, TCRT13.D+, TCRT14.D+, TCRT15.D+, TCRT16.D+, Part2.5V
  N4: TCRT9.T+, Part2.A3
  N5: TCRT10.T+, Part2.A2
  N6: TCRT11.T+, Part2.A4
  N7: TCRT12.T+, Part2.A5
  N8: TCRT13.T+, Part2.A6
  N9: TCRT14.T+, Part2.A1
  N10: TCRT15.T+, Part2.A0
  N11: TCRT16.T+, Part2.A7
  N12: S1.OUT4-Motor2, M2.pin_1
  N13: S1.OUT1-Motor1, M3.pin_1
  N14: S1.OUT2-Motor1, M3.pin_2
  N15: U1.+, U2.-
  N16: U2.+, U3.-

custom parts:
  TCRT5000 sensor module: breakout board with TCRT5000
  H-Bridge with L298N: h-bridge
